# Fritzing sketch IR Send (saved by Fritzing 0.9.3b)
breadboards: 1

parts:
  WeMos_D1_Mini1 = WeMos D1 Mini  # not connected
  2N3904 = PNP-Transistor [package="SOT-23 [SMD]"]
  LED2 = LED - 5mm [color="White (4500K)" package="5 mm [THT]"]
  part = Resistor [tolerance=±5% resistance=1k package=THT]
  part_2 = Resistor [tolerance=±5% resistance=20 package=THT]

nets:
  N1: 2N3904.0, part.Pin_0
  N2: 2N3904.1, LED2.cathode
  N3: LED2.anode, part_2.Pin_0
